// Logisim project Master-Cleaned.circ as structural Verilog: 7 circuits, main circuit main
module main (
  output Halt,
  output [7:0] out_2,
  output [7:0] out_3,
  output [7:0] out_4,
  output [7:0] out_5,
  output [7:0] out_6,
  output [7:0] out_7,
  output [7:0] out_8,
  output [7:0] out_9,
  output [7:0] out_10
);

  wire addrEnable, Clock, comparator_1_eq, comparator_2_eq, comparator_3_eq, comparator_4_eq, decoder_1_out3,
       decoder_1_out4, decoder_1_out5, decoder_1_out6, decoder_2_out3, decoder_2_out4, Dest_Enabler, Group_0,
       Group_1, Group_2, Group_3, Group_4, Group_5, jump_e, ld_enable, Load_Enable, not_1_out, not_2_out,
       not_3_out, not_4_out, not_5_out, not_6_out, not_7_out, not_8_out, not_9_out, not_10_out, not_11_out,
       not_12_out, not_13_out, not_14_out, not_15_out, not_16_out, not_17_out, not_18_out, not_19_out,
       not_20_out, not_21_out, not_22_out, or_1_out, or_2_out, or_4_out, or_5_out, or_9_out, RMov_Enable,
       Src_Enabler, st_enable, ZF;
  wire [3:0] Dest_4_load, Group, IB, Instruction, multiplexer_2_out, multiplexer_5_out;
  wire [7:0] Address, alu_1_alu_output, DB, Dest_disp, Dest_Mem_Adress, multiplexer_1_out, multiplexer_4_out,
       multiplexer_7_out, pc_1_pc_out, RA_Disp, RegA, RegB, Source_Mem_Adress, Src_Disp;
  wire [23:0] bit_extender_1_out;

  or or_1 (or_1_out, addrEnable, Load_Enable);
  not not_1 (not_1_out, or_1_out);
  Clock clock_1 (.out(Clock));
  or or_2 (or_2_out, Group_2, RMov_Enable, Group_5, Group_4, Group_3);
  Multiplexer #(.select(4), .width(8), .enable("false")) multiplexer_1 (
    .in3(RA_Disp), .in4(Source_Mem_Adress), .in5(Dest_Mem_Adress), .in6(out_2), .in10(Source_Mem_Adress),
    .in11(Source_Mem_Adress), .out(multiplexer_1_out), .sel(Instruction));  // open: in0, in1, in2, in7, in8, in9, in12, in13, in14, in15
  PC pc_1 (
    .HALT(Halt), .Address(Address), .Increment(not_1_out), .in_1(Clock), .Enabler(or_1_out), .Inst(IB),
    .PC_Out(pc_1_pc_out));  // open: out_7
  Multiplexer #(.select(4), .width(4)) multiplexer_2 (
    .in0(Instruction), .in1(Instruction), .in2(Instruction), .in3(IB), .in4(IB), .in5(Instruction),
    .in6(Instruction), .in7(Instruction), .in8(Instruction), .in9(Instruction), .in10(Instruction),
    .in11(Instruction), .in12(Instruction), .in13(Instruction), .in14(Instruction), .in15(Instruction),
    .out(multiplexer_2_out), .sel(IB));  // open: en
  Register u_Address (.Clock(not_3_out), .Enable(addrEnable), .Input(multiplexer_1_out), .Output(Address));
  assign bit_extender_1_out = {{16{1'b0}}, DB};  // Bit_Extender bit_extender_1
  not not_2 (not_2_out, ld_enable);
  or or_3 (addrEnable, jump_e, Group_3, Group_5);
  not not_3 (not_3_out, Clock);
  Multiplexer #(.select(4), .width(8)) multiplexer_3 (
    .in1(out_3), .in2(out_4), .in3(out_5), .in4(out_6), .in5(out_7), .in6(out_8), .in7(out_9), .in8(out_10),
    .out(RegA), .sel(Source_Mem_Adress[3:0]), .en(or_2_out));  // open: in0, in9, in10, in11, in12, in13, in14, in15
  Multiplexer #(.select(4), .width(8)) multiplexer_4 (
    .in1(Source_Mem_Adress), .in2(RegA), .in3(Dest_Mem_Adress), .in4(Dest_Mem_Adress), .in5(RegA),
    .in6(RegA), .in7(RegA), .in8(RegA), .in9(RegA), .in10(RegA), .out(multiplexer_4_out),
    .sel(multiplexer_2_out), .en(not_2_out));  // open: in0, in11, in12, in13, in14, in15
  not not_4 (not_4_out, Clock);
  not not_5 (not_5_out, Clock);
  RAM #(.dataWidth(24), .bus("separate")) ram_1 (
    .addr(pc_1_pc_out), .din(bit_extender_1_out),
    .data({Group, Instruction, Source_Mem_Adress, Dest_Mem_Adress}), .str(st_enable), .clk(Clock));  // open: sel, ld, clr
  ALU alu_1 (
    .RA(multiplexer_4_out), .RB(RegB), .Instruction(Instruction), .Clock(Clock),
    .ALU_Output(alu_1_alu_output), .Data(DB), .ZF(ZF));
  IB ib_1 (.Clock(not_4_out), .Instruction(Instruction), .Data(IB));
  IB ib_2 (.Clock(not_5_out), .Instruction(Dest_Mem_Adress[3:0]), .Data(Dest_4_load));
  or or_4 (or_4_out, Group_2, Group_1, Group_3);
  Multiplexer #(.select(4), .width(4)) multiplexer_5 (
    .in0(Dest_Mem_Adress[3:0]), .in1(Dest_Mem_Adress[3:0]), .in2(Dest_Mem_Adress[3:0]), .in3(Dest_4_load),
    .in4(Dest_4_load), .in5(Dest_4_load), .in6(Dest_4_load), .in7(Dest_Mem_Adress[3:0]),
    .in8(Dest_Mem_Adress[3:0]), .in9(Dest_Mem_Adress[3:0]), .in10(Dest_Mem_Adress[3:0]),
    .in11(Dest_Mem_Adress[3:0]), .in12(Dest_Mem_Adress[3:0]), .in13(Dest_Mem_Adress[3:0]),
    .in14(Dest_Mem_Adress[3:0]), .in15(Dest_Mem_Adress[3:0]), .out(multiplexer_5_out), .sel(IB));  // open: en
  Comparator #(.width(4)) comparator_1 (.a(IB), .b(4'b0011), .eq(comparator_1_eq));  // open: gt, lt
  Comparator #(.width(4)) comparator_2 (.a(IB), .b(4'b0100), .eq(comparator_2_eq));  // open: gt, lt
  Do_Jump do_jump_1 (.Instruction(Instruction), .ZF(ZF), .jump_enable(jump_e));
  Multiplexer #(.select(4), .width(8)) multiplexer_6 (
    .in1(out_3), .in2(out_4), .in3(out_5), .in4(out_6), .in5(out_7), .in6(out_8), .in7(out_9), .in8(out_10),
    .out(RegB), .sel(Dest_Mem_Adress[3:0]), .en(or_4_out));  // open: in0, in9, in10, in11, in12, in13, in14, in15
  Multiplexer #(.width(8)) multiplexer_7 (
    .in0(alu_1_alu_output), .in1(Dest_Mem_Adress), .out(multiplexer_7_out), .sel(or_5_out));  // open: en
  or or_5 (or_5_out, comparator_1_eq, comparator_2_eq);
  Decoder #(.select(4)) decoder_1 (
    .out3(decoder_1_out3), .out4(decoder_1_out4), .out5(decoder_1_out5), .out6(decoder_1_out6), .sel(IB));  // open: out0, out1, out2, out7, out8, out9, out10, out11, out12, out13, out14, out15, en
  or or_6 (Load_Enable, decoder_1_out3, decoder_1_out4, decoder_1_out5, decoder_1_out6);
  not not_6 (not_6_out, Group[0]);
  not not_7 (not_7_out, Group[1]);
  and and_1 (Group_0, not_6_out, not_7_out, not_11_out, not_8_out);
  Register_Bank register_bank_1 (
    .Dest_Enabler(Dest_Enabler), .Destination(multiplexer_5_out), .ALU_Output(multiplexer_7_out),
    .Clock(Clock), .R0(out_3), .R1(out_4), .R2(out_5), .R3(out_6), .R4(out_7), .R5(out_8), .R6(out_9),
    .R7(out_10));
  or or_7 (st_enable, decoder_1_out5, decoder_1_out6);
  not not_8 (not_8_out, Group[3]);
  not not_9 (not_9_out, Group[1]);
  not not_10 (not_10_out, Group[2]);
  not not_11 (not_11_out, Group[2]);
  not not_12 (not_12_out, Group[3]);
  and and_2 (Group_1, Group[0], not_9_out, not_10_out, not_12_out);
  not not_13 (not_13_out, Group[3]);
  not not_14 (not_14_out, Group[0]);
  not not_15 (not_15_out, Group[2]);
  and and_3 (Group_2, not_14_out, Group[1], not_15_out, not_13_out);
  assign Dest_disp = {{4{1'b0}}, Dest_Mem_Adress[7:4]};  // Bit_Extender bit_extender_2
  assign Src_Disp = {{4{1'b0}}, Source_Mem_Adress[7:4]};  // Bit_Extender bit_extender_3
  Decoder #(.select(4)) decoder_2 (
    .out2(RMov_Enable), .out3(decoder_2_out3), .out4(decoder_2_out4), .out15(Halt), .sel(Instruction));  // open: out0, out1, out5, out6, out7, out8, out9, out10, out11, out12, out13, out14, en
  or or_8 (ld_enable, decoder_2_out3, decoder_2_out4);
  not not_16 (not_16_out, Group[3]);
  not not_17 (not_17_out, Group[1]);
  not not_18 (not_18_out, Group[2]);
  not not_19 (not_19_out, Group[0]);
  and and_4 (Group_3, Group[0], Group[1], not_18_out, not_16_out);
  and and_5 (Group_4, not_19_out, not_17_out, Group[2], not_22_out);
  not not_20 (not_20_out, Group[1]);
  not not_21 (not_21_out, Group[3]);
  not not_22 (not_22_out, Group[3]);
  and and_6 (Group_5, Group[0], not_20_out, Group[2], not_21_out);
  Adder adder_1 (.a(RegA), .b(Src_Disp), .out(RA_Disp));  // open: cin, cout
  Adder adder_2 (.a(RegB), .b(Dest_disp), .out(out_2));  // open: cin, cout
  Comparator #(.width(4)) comparator_3 (.a(IB), .b(4'b0011), .eq(comparator_3_eq));  // open: gt, lt
  Comparator #(.width(4)) comparator_4 (.a(IB), .b(4'b0100), .eq(comparator_4_eq));  // open: gt, lt
  or or_9 (or_9_out, comparator_3_eq, comparator_4_eq);
  or or_10 (Src_Enabler, Group_2, Group_4, Group_3);
  or or_11 (Dest_Enabler, Group_2, Group_1, or_9_out);

  // Other names for the same wires on the sheet: Destination[3:0] = Dest_Mem_Adress[3:0];
  //   mem_data[7:0] = Dest_Mem_Adress; R0[7:0] = out_3; R1[7:0] = out_4; R2[7:0] = out_5; R3[7:0] = out_6;
  //   R4[7:0] = out_7; R5[7:0] = out_8; R6[7:0] = out_9; R7[7:0] = out_10; RB_Disp[7:0] = out_2

  // Notes on the sheet:
  //   Control Unit
  //   Buses
  //   Inputs
  //   halt
  //   IRMov
  //   help
  //   Displacement
  //   Register Outputs
  //   Enablers
endmodule

module Register_Bank (
  input  Dest_Enabler,
  input  [3:0] Destination,
  input  Clock,
  input  [7:0] ALU_Output,
  output [7:0] R0,
  output [7:0] R1,
  output [7:0] R2,
  output [7:0] R3,
  output [7:0] R4,
  output [7:0] R5,
  output [7:0] R6,
  output [7:0] R7
);

  wire and_1_out, and_2_out, and_3_out, and_4_out, and_5_out, and_6_out, and_7_out, and_8_out,
       decoder_1_out1, decoder_1_out2, decoder_1_out3, decoder_1_out4, decoder_1_out5, decoder_1_out6,
       decoder_1_out7, decoder_1_out8, not_1_out;

  Decoder #(.select(4)) decoder_1 (
    .out1(decoder_1_out1), .out2(decoder_1_out2), .out3(decoder_1_out3), .out4(decoder_1_out4),
    .out5(decoder_1_out5), .out6(decoder_1_out6), .out7(decoder_1_out7), .out8(decoder_1_out8),
    .sel(Destination), .en(Dest_Enabler));  // open: out0, out9, out10, out11, out12, out13, out14, out15
  not not_1 (not_1_out, Clock);
  and and_1 (and_1_out, not_1_out, decoder_1_out1);
  and and_2 (and_2_out, not_1_out, decoder_1_out2);
  and and_3 (and_3_out, not_1_out, decoder_1_out3);
  and and_4 (and_4_out, not_1_out, decoder_1_out4);
  and and_5 (and_5_out, not_1_out, decoder_1_out5);
  and and_6 (and_6_out, not_1_out, decoder_1_out6);
  and and_7 (and_7_out, not_1_out, decoder_1_out7);
  and and_8 (and_8_out, not_1_out, decoder_1_out8);
  Register u_R0 (.Clock(and_1_out), .Enable(decoder_1_out1), .Input(ALU_Output), .Output(R0));
  Register u_R1 (.Clock(and_2_out), .Enable(decoder_1_out2), .Input(ALU_Output), .Output(R1));
  Register u_R2 (.Clock(and_3_out), .Enable(decoder_1_out3), .Input(ALU_Output), .Output(R2));
  Register u_R3 (.Clock(and_4_out), .Enable(decoder_1_out4), .Input(ALU_Output), .Output(R3));
  Register u_R4 (.Clock(and_5_out), .Enable(decoder_1_out5), .Input(ALU_Output), .Output(R4));
  Register u_R5 (.Clock(and_6_out), .Enable(decoder_1_out6), .Input(ALU_Output), .Output(R5));
  Register u_R6 (.Clock(and_7_out), .Enable(decoder_1_out7), .Input(ALU_Output), .Output(R6));
  Register u_R7 (.Clock(and_8_out), .Enable(decoder_1_out8), .Input(ALU_Output), .Output(R7));
endmodule

module Register (
  input  Clock,
  input  Enable,
  input  [7:0] Input,
  output [7:0] Output
);

  D_Flip_Flop d_ff_1 (.clk(Clock), .D(Input[0]), .Q(Output[0]), .en(Enable));  // open: Qn, preset, reset
  D_Flip_Flop d_ff_2 (.clk(Clock), .D(Input[1]), .Q(Output[1]), .en(Enable));  // open: Qn, preset, reset
  D_Flip_Flop d_ff_3 (.clk(Clock), .D(Input[2]), .Q(Output[2]), .en(Enable));  // open: Qn, preset, reset
  D_Flip_Flop d_ff_4 (.clk(Clock), .D(Input[3]), .Q(Output[3]), .en(Enable));  // open: Qn, preset, reset
  D_Flip_Flop d_ff_5 (.clk(Clock), .D(Input[4]), .Q(Output[4]), .en(Enable));  // open: Qn, preset, reset
  D_Flip_Flop d_ff_6 (.clk(Clock), .D(Input[5]), .Q(Output[5]), .en(Enable));  // open: Qn, preset, reset
  D_Flip_Flop d_ff_7 (.clk(Clock), .D(Input[6]), .Q(Output[6]), .en(Enable));  // open: Qn, preset, reset
  D_Flip_Flop d_ff_8 (.clk(Clock), .D(Input[7]), .Q(Output[7]), .en(Enable));  // open: Qn, preset, reset
endmodule

module ALU (
  input  [7:0] RA,
  input  [7:0] RB,
  input  [3:0] Instruction,
  input  Clock,
  output [7:0] ALU_Output,
  output [7:0] Data,
  output ZF
);

  wire not_1_out;
  wire [7:0] adder_1_out, multiplier_1_out, subtractor_1_out;

  Adder adder_1 (.a(RA), .b(RB), .out(adder_1_out));  // open: cin, cout
  Multiplexer #(.select(4), .width(8), .enable("false")) multiplexer_1 (
    .in1(RA), .in2(RA), .in3(RA), .in4(Data), .in5(RA), .in6(RA), .in7(adder_1_out), .in8(subtractor_1_out),
    .in9(multiplier_1_out), .in10(Data), .in11(Data), .out(ALU_Output), .sel(Instruction));  // open: in0, in12, in13, in14, in15
  not not_1 (not_1_out, Clock);
  Subtractor subtractor_1 (.a(RA), .b(RB), .out(subtractor_1_out));  // open: bin, bout
  Register u_Data (.Clock(not_1_out), .Enable(1'b1), .Input(ALU_Output), .Output(Data));
  Multiplier multiplier_1 (.a(RA), .b(RB), .out(multiplier_1_out));  // open: cin, cout
  Comparator comparator_1 (.a(Data), .b({8{1'b0}}), .eq(ZF));  // open: gt, lt

  // Other names for the same wires on the sheet: ALU_out[7:0] = ALU_Output; Reg_out[7:0] = Data

  // Notes on the sheet:
  //   Source
  //   Destination
  //   Register Values
  //   irmov
  //   rrmov
  //   Add
  //   Sub
  //   Mul
endmodule

module PC (
  input  in_1,
  input  HALT,
  input  Enabler,
  input  [7:0] Address,
  input  Increment,
  input  [3:0] Inst,
  output [7:0] out_7,
  output [7:0] PC_Out
);

  wire and_1_out;
  wire [7:0] multiplexer_1_out, register_1_output;

  and and_1 (and_1_out, ~HALT, in_1);  // AND_Gate
  Multiplexer #(.select(4), .width(8), .enable("false")) multiplexer_1 (
    .in0(Address), .in1(Address), .in2(Address), .in3(out_7), .in4(out_7), .in5(out_7), .in6(out_7),
    .in7(Address), .in8(Address), .in9(Address), .in10(Address), .in11(Address), .in12(Address),
    .in13(Address), .in14(Address), .out(multiplexer_1_out), .sel(Inst));  // open: in15
  Counter counter_1 (
    .load(Enabler), .D(multiplexer_1_out), .count(Increment), .Q(PC_Out), .clk(and_1_out));  // open: carry, clr
  Register register_1 (.Clock(in_1), .Enable(1'b1), .Input(PC_Out), .Output(register_1_output));
  Adder adder_1 (.a(register_1_output), .b(8'h1), .out(out_7));  // open: cin, cout

  // Other names for the same wires on the sheet: Clock = in_1; PC[7:0] = PC_Out; PC_Bus[7:0] = out_7
endmodule

module Do_Jump (
  input  [3:0] Instruction,
  input  ZF,
  output jump_enable
);

  wire and_1_out, and_2_out, not_1_out, not_2_out;

  not not_1 (not_1_out, Instruction[0]);
  not not_2 (not_2_out, Instruction[2]);
  and and_1 (and_1_out, not_1_out, Instruction[1], not_2_out, Instruction[3]);
  and and_2 (and_2_out, Instruction[0], Instruction[1], not_2_out, Instruction[3], ZF);
  or or_1 (jump_enable, and_1_out, and_2_out);

  // Notes on the sheet:
  //   If jmp
  //   If jz and ZF set
endmodule

module IB (
  input  Clock,
  input  [3:0] Instruction,
  output [3:0] Data
);

  wire not_1_out;
  wire [7:0] bit_extender_1_out;
  wire [7:4] IB_output;

  assign bit_extender_1_out = {{4{1'b0}}, Instruction};  // Bit_Extender bit_extender_1
  not not_1 (not_1_out, Clock);
  Register IB (.Clock(not_1_out), .Enable(1'b1), .Input(bit_extender_1_out), .Output({IB_output, Data}));
endmodule
