// Logisim project Master-v2.circ as structural Verilog: 6 circuits, main circuit main
module main (
  output [7:0] DMem_Adress,
  output [3:0] Source,
  output Source_Enabler,
  output [7:0] out_4,
  output [7:0] SMem_Adress,
  output [7:0] out_6,
  output [7:0] out_7,
  output [7:0] out_8,
  output [3:0] Instruction,
  output Halt,
  output [7:0] out_11,
  output [7:0] out_12,
  output [7:0] out_13,
  output Clock,
  output [7:0] out_15,
  output [7:0] out_16,
  output [7:0] out_17
);

  wire Dest_Enabler, Group_0, Group_1, Group_2, Group_3, Group_4, not_1_out, not_2_out, not_3_out, not_4_out,
       not_5_out, not_6_out, not_7_out, not_8_out, not_9_out, not_10_out, not_11_out, not_12_out, not_13_out,
       not_14_out, not_15_out, or_3_out, or_4_out, Subtract_On;
  wire [3:0] Group;
  wire [4:0] pc_1_count;
  wire [7:0] multiplexer_1_out, RegB;

  PC pc_1 (.Count(pc_1_count), .HALT(Halt), .Clock(Clock));
  not not_1 (not_1_out, Group[3]);
  not not_2 (not_2_out, Group[1]);
  not not_3 (not_3_out, Group[0]);
  not not_4 (not_4_out, Group[1]);
  not not_5 (not_5_out, Group[2]);
  and and_1 (Group_0, not_3_out, not_4_out, not_5_out, not_1_out);
  LED led_1 (.in(Group_0));
  not not_6 (not_6_out, Group[3]);
  not not_7 (not_7_out, Group[2]);
  not not_8 (not_8_out, Group[2]);
  not not_9 (not_9_out, Group[0]);
  and and_2 (Group_2, not_9_out, Group[1], not_8_out, not_12_out);
  and and_3 (Group_1, Group[0], not_2_out, not_7_out, not_6_out);
  LED led_2 (.in(Group_2));
  LED led_3 (.in(Group_1));
  ROM #(.addrWidth(5), .dataWidth(24)) rom_1 (
    .addr(pc_1_count), .data({Group, Instruction, SMem_Adress, DMem_Adress}));  // open: sel
  not not_10 (not_10_out, Group[2]);
  not not_11 (not_11_out, Group[3]);
  not not_12 (not_12_out, Group[3]);
  and and_4 (Group_3, Group[0], Group[1], not_10_out, not_11_out);
  LED led_4 (.in(Group_3));
  not not_13 (not_13_out, Group[0]);
  not not_14 (not_14_out, Group[1]);
  not not_15 (not_15_out, Group[3]);
  and and_5 (Group_4, not_13_out, not_14_out, Group[2], not_15_out);
  LED led_5 (.in(Group_4));
  Multiplexer #(.select(4), .width(8), .enable("false")) multiplexer_1 (
    .in1(SMem_Adress), .in2(out_17), .in3(out_17), .in4(out_17), .out(multiplexer_1_out), .sel(Group));  // open: in0, in5, in6, in7, in8, in9, in10, in11, in12, in13, in14, in15
  ALU alu_1 (
    .RA(multiplexer_1_out), .RB(RegB), .Instruction(Instruction), .Dest_Enabler(Dest_Enabler),
    .ALU_Output(out_16));  // open: Sub_Enabler, ldr, ldm, stm, str, Jmp, jz
  Register_Bank register_bank_1 (
    .Dest_Enabler(Dest_Enabler), .Destination(DMem_Adress[3:0]), .ALU_Output(out_16), .Clock(Clock),
    .R0(out_4), .R1(out_6), .R2(out_7), .R3(out_8), .R4(out_11), .R5(out_12), .R6(out_13), .R7(out_15));
  Decoder #(.select(4)) decoder_1 (
    .out0(Halt), .out8(Subtract_On), .sel(Instruction));  // open: out1, out2, out3, out4, out5, out6, out7, out9, out10, out11, out12, out13, out14, out15, en
  or or_1 (Dest_Enabler, Group_2, Group_1, Group_3);
  or or_2 (Source_Enabler, Group_2, Group_4, Group_3);
  or or_3 (or_3_out, Group_2, Group_4, Group_3);
  or or_4 (or_4_out, Group_2, Group_1, Group_3);
  Multiplexer #(.select(4), .width(8)) multiplexer_2 (
    .in1(out_4), .in2(out_6), .in3(out_7), .in4(out_8), .in5(out_11), .in6(out_12), .in7(out_13),
    .in8(out_15), .out(out_17), .sel(SMem_Adress[3:0]), .en(or_3_out));  // open: in0, in9, in10, in11, in12, in13, in14, in15
  Multiplexer #(.select(4), .width(8)) multiplexer_3 (
    .in1(out_4), .in2(out_6), .in3(out_7), .in4(out_8), .in5(out_11), .in6(out_12), .in7(out_13),
    .in8(out_15), .out(RegB), .sel(DMem_Adress[3:0]), .en(or_4_out));  // open: in0, in9, in10, in11, in12, in13, in14, in15

  assign Source = SMem_Adress[3:0];

  // Other names for the same wires on the sheet: Dest_Mem_Adress[7:0] = DMem_Adress;
  //   Source_Mem_Adress[7:0] = SMem_Adress; Destination[3:0] = DMem_Adress[3:0]; R0[7:0] = out_4; R1[7:0] = out_6;
  //   R2[7:0] = out_7; R3[7:0] = out_8; R4[7:0] = out_11; R5[7:0] = out_12; R6[7:0] = out_13; R7[7:0] = out_15;
  //   RegA[7:0] = out_17

  // Notes on the sheet:
  //   halt
  //   IRMov
  //   contents of rom_1 (hex, n*v repeats v):
  //   ffffff 115c07 110304 270407 220604 4bff00 4a1b00 280301 330203 5407ab 360408 5505bf 270102 290805
  //   help
  //   Dest Enabler
endmodule

module Register_Bank (
  input  Dest_Enabler,
  input  [3:0] Destination,
  input  Clock,
  input  [7:0] ALU_Output,
  output [7:0] R0,
  output [7:0] R1,
  output [7:0] R2,
  output [7:0] R3,
  output [7:0] R4,
  output [7:0] R5,
  output [7:0] R6,
  output [7:0] R7
);

  wire and_1_out, and_2_out, and_3_out, and_4_out, and_5_out, and_6_out, and_7_out, and_8_out,
       decoder_1_out1, decoder_1_out2, decoder_1_out3, decoder_1_out4, decoder_1_out5, decoder_1_out6,
       decoder_1_out7, decoder_1_out8, not_1_out;

  Decoder #(.select(4)) decoder_1 (
    .out1(decoder_1_out1), .out2(decoder_1_out2), .out3(decoder_1_out3), .out4(decoder_1_out4),
    .out5(decoder_1_out5), .out6(decoder_1_out6), .out7(decoder_1_out7), .out8(decoder_1_out8),
    .sel(Destination), .en(Dest_Enabler));  // open: out0, out9, out10, out11, out12, out13, out14, out15
  not not_1 (not_1_out, Clock);
  and and_1 (and_1_out, not_1_out, decoder_1_out1);
  and and_2 (and_2_out, not_1_out, decoder_1_out2);
  and and_3 (and_3_out, not_1_out, decoder_1_out3);
  and and_4 (and_4_out, not_1_out, decoder_1_out4);
  and and_5 (and_5_out, not_1_out, decoder_1_out5);
  and and_6 (and_6_out, not_1_out, decoder_1_out6);
  and and_7 (and_7_out, not_1_out, decoder_1_out7);
  and and_8 (and_8_out, not_1_out, decoder_1_out8);
  Register u_R0 (.in_1(and_1_out), .Enable(decoder_1_out1), .Input(ALU_Output), .out_4(R0));
  Register u_R1 (.in_1(and_2_out), .Enable(decoder_1_out2), .Input(ALU_Output), .out_4(R1));
  Register u_R2 (.in_1(and_3_out), .Enable(decoder_1_out3), .Input(ALU_Output), .out_4(R2));
  Register u_R3 (.in_1(and_4_out), .Enable(decoder_1_out4), .Input(ALU_Output), .out_4(R3));
  Register u_R4 (.in_1(and_5_out), .Enable(decoder_1_out5), .Input(ALU_Output), .out_4(R4));
  Register u_R5 (.in_1(and_6_out), .Enable(decoder_1_out6), .Input(ALU_Output), .out_4(R5));
  Register u_R6 (.in_1(and_7_out), .Enable(decoder_1_out7), .Input(ALU_Output), .out_4(R6));
  Register u_R7 (.in_1(and_8_out), .Enable(decoder_1_out8), .Input(ALU_Output), .out_4(R7));
endmodule

module Register (
  input  in_1,
  input  Enable,
  input  [7:0] Input,
  output [7:0] out_4
);

  D_Flip_Flop d_ff_1 (.clk(in_1), .D(Input[0]), .Q(out_4[0]), .en(Enable));  // open: Qn, preset, reset
  D_Flip_Flop d_ff_2 (.clk(in_1), .D(Input[1]), .Q(out_4[1]), .en(Enable));  // open: Qn, preset, reset
  D_Flip_Flop d_ff_3 (.clk(in_1), .D(Input[2]), .Q(out_4[2]), .en(Enable));  // open: Qn, preset, reset
  D_Flip_Flop d_ff_4 (.clk(in_1), .D(Input[3]), .Q(out_4[3]), .en(Enable));  // open: Qn, preset, reset
  D_Flip_Flop d_ff_5 (.clk(in_1), .D(Input[4]), .Q(out_4[4]), .en(Enable));  // open: Qn, preset, reset
  D_Flip_Flop d_ff_6 (.clk(in_1), .D(Input[5]), .Q(out_4[5]), .en(Enable));  // open: Qn, preset, reset
  D_Flip_Flop d_ff_7 (.clk(in_1), .D(Input[6]), .Q(out_4[6]), .en(Enable));  // open: Qn, preset, reset
  D_Flip_Flop d_ff_8 (.clk(in_1), .D(Input[7]), .Q(out_4[7]), .en(Enable));  // open: Qn, preset, reset
endmodule

module ALU (
  input  [7:0] RA,
  input  [7:0] RB,
  input  Sub_Enabler,
  input  str,
  input  stm,
  input  ldm,
  input  ldr,
  input  Jmp,
  input  jz,
  input  [3:0] Instruction,
  input  Dest_Enabler,
  output [7:0] ALU_Output
);

  wire [7:0] adder_1_out, multiplier_1_out, subtractor_1_out;
  wire [7:1] undriven, undriven_2, undriven_3, undriven_4, undriven_5, undriven_6;

  Adder adder_1 (.a(RA), .b(RB), .out(adder_1_out));  // open: cin, cout
  Multiplexer #(.select(4), .width(8)) multiplexer_1 (
    .in1(RA), .in2(RA), .in3({undriven, ldr}), .in4({undriven_2, ldm}), .in5({undriven_3, stm}),
    .in6({undriven_4, str}), .in7(adder_1_out), .in8(subtractor_1_out), .in9(multiplier_1_out),
    .in10({undriven_5, Jmp}), .in11({undriven_6, jz}), .out(ALU_Output), .sel(Instruction), .en(Dest_Enabler));  // open: in0, in12, in13, in14, in15
  Subtractor subtractor_1 (.a(RA), .b(RB), .out(subtractor_1_out));  // open: bin, bout
  Multiplier multiplier_1 (.a(RA), .b(RB), .out(multiplier_1_out));  // open: cin, cout
  // Pins of 1 and 8 bits meet at {undriven_3, stm}
  // Pins of 1 and 8 bits meet at {undriven, ldr}
  // Pins of 1 and 8 bits meet at {undriven_2, ldm}
  // Pins of 1 and 8 bits meet at {undriven_4, str}
  // Pins of 1 and 8 bits meet at {undriven_5, Jmp}
  // Pins of 1 and 8 bits meet at {undriven_6, jz}

  // Notes on the sheet:
  //   Source
  //   Destination
  //   Register Values
  //   irmov
  //   rrmov
  //   Add
  //   Sub
  //   Mul
endmodule

module PC (
  input  HALT,
  output Clock,
  output [4:0] Count
);

  wire and_1_out, t_ff_1_qn, t_ff_2_qn, t_ff_3_qn, t_ff_4_qn;

  T_Flip_Flop t_ff_1 (.clk(and_1_out), .T(1'b1), .Q(Count[0]), .Qn(t_ff_1_qn));  // open: preset, reset, en
  Clock clock_1 (.out(Clock));
  and and_1 (and_1_out, ~HALT, Clock);  // AND_Gate
  T_Flip_Flop t_ff_2 (.clk(t_ff_1_qn), .T(1'b1), .Q(Count[1]), .Qn(t_ff_2_qn));  // open: preset, reset, en
  T_Flip_Flop t_ff_3 (.clk(t_ff_2_qn), .T(1'b1), .Q(Count[2]), .Qn(t_ff_3_qn));  // open: preset, reset, en
  T_Flip_Flop t_ff_4 (.clk(t_ff_3_qn), .T(1'b1), .Q(Count[3]), .Qn(t_ff_4_qn));  // open: preset, reset, en
  T_Flip_Flop t_ff_5 (.clk(t_ff_4_qn), .T(1'b1), .Q(Count[4]));  // open: Qn, preset, reset, en
endmodule

module Add_and_Subtract (
  input  Sub_Enabler,
  input  [7:0] RA,
  input  [7:0] RB
);
endmodule
