// Logisim project Master-v4.circ as structural Verilog: 7 circuits, main circuit main
module main (
  output Halt,
  output [3:0] Source,
  output Source_Enabler,
  output [7:0] out_4,
  output [7:0] SMem_Adress,
  output [7:0] out_6,
  output [7:0] out_7,
  output [7:0] out_8,
  output [3:0] Instruction,
  output [7:0] out_10,
  output [7:0] out_11,
  output [7:0] out_12,
  output [7:0] out_13,
  output [7:0] Data_Bus,
  output [7:0] out_15,
  output [7:0] RagA,
  output [3:0] IB,
  output [3:0] IB_2,
  output [7:0] Adress_Bus,
  output ld_enable,
  output st_enable
);

  wire addrEnable, Clock, decoder_1_out3, decoder_1_out4, decoder_1_out5, decoder_1_out6, Dest_Enabler,
       Group_0, Group_1, Group_2, Group_3, Group_4, Group_5, jump_e, not_1_out, not_2_out, not_3_out,
       not_4_out, not_5_out, not_6_out, not_7_out, not_8_out, not_9_out, not_10_out, not_11_out, not_12_out,
       not_13_out, not_14_out, not_15_out, not_16_out, not_17_out, not_18_out, not_19_out, not_20_out,
       or_1_out, or_7_out, or_8_out, RMov_Enable, ZF;
  wire [3:0] Group, multiplexer_3_out;
  wire [7:0] Dest_Mem_Adress, multiplexer_1_out, multiplexer_2_out, pc_1_pc, RegB;

  or or_1 (or_1_out, st_enable, ld_enable);
  PC pc_1 (.HALT(Halt), .Clock(Clock), .Enabler(addrEnable), .Address(Adress_Bus), .LD_Enable(or_1_out), .PC(pc_1_pc));
  IB ib_1 (.Clock(not_1_out), .Instruction(Instruction), .Data(IB));
  not not_1 (not_1_out, Clock);
  IB u_ib_2 (.Clock(not_2_out), .Instruction(Dest_Mem_Adress[3:0]), .Data(IB_2));
  not not_2 (not_2_out, Clock);
  not not_3 (not_3_out, Group[1]);
  not not_4 (not_4_out, Group[3]);
  not not_5 (not_5_out, Group[2]);
  not not_6 (not_6_out, Group[0]);
  not not_7 (not_7_out, Group[1]);
  and and_1 (Group_0, not_6_out, not_7_out, not_5_out, not_4_out);
  LED led_1 (.in(Group_0));
  not not_8 (not_8_out, Group[2]);
  not not_9 (not_9_out, Group[3]);
  not not_10 (not_10_out, Group[0]);
  not not_11 (not_11_out, Group[2]);
  and and_2 (Group_2, not_10_out, Group[1], not_8_out, not_13_out);
  and and_3 (Group_1, Group[0], not_3_out, not_11_out, not_9_out);
  LED led_2 (.in(Group_2));
  LED led_3 (.in(Group_1));
  RAM #(.dataWidth(24), .bus("separate")) ram_1 (
    .addr(pc_1_pc), .data({Group, Instruction, SMem_Adress, Dest_Mem_Adress}), .str(st_enable), .clk(Clock));  // open: din, sel, ld, clr
  not not_12 (not_12_out, Group[3]);
  not not_13 (not_13_out, Group[3]);
  not not_14 (not_14_out, Group[2]);
  and and_4 (Group_3, Group[0], Group[1], not_14_out, not_12_out);
  LED led_4 (.in(Group_3));
  not not_15 (not_15_out, Group[0]);
  not not_16 (not_16_out, Group[1]);
  not not_17 (not_17_out, Group[3]);
  not not_18 (not_18_out, Group[1]);
  and and_5 (Group_4, not_15_out, not_18_out, Group[2], not_17_out);
  LED led_5 (.in(Group_4));
  Multiplexer #(.select(4), .width(8)) multiplexer_1 (
    .in1(SMem_Adress), .in2(RagA), .in3({Instruction, Group}), .in4({Instruction, Group}), .in5(RagA),
    .in6(RagA), .in7(RagA), .in8(RagA), .in9(RagA), .in10(RagA), .out(multiplexer_1_out), .sel(Instruction));  // open: in0, in11, in12, in13, in14, in15, en
  Multiplexer #(.select(4), .width(8), .enable("false")) multiplexer_2 (
    .in4(SMem_Adress), .in5(SMem_Adress), .out(multiplexer_2_out), .sel(Group));  // open: in0, in1, in2, in3, in6, in7, in8, in9, in10, in11, in12, in13, in14, in15
  not not_19 (not_19_out, Group[3]);
  and and_6 (Group_5, Group[0], not_16_out, Group[2], not_19_out);
  LED led_6 (.in(Group_5));
  ALU alu_1 (
    .RA(multiplexer_1_out), .RB(RegB), .Instruction(Instruction), .ld_enable(ld_enable), .Clock(Clock),
    .ALU_Output(out_15), .Data(Data_Bus), .ZF(ZF));  // open: str
  Multiplexer #(.select(4), .width(4)) multiplexer_3 (
    .in1(Dest_Mem_Adress[3:0]), .in2(Dest_Mem_Adress[3:0]), .in3(IB_2), .in4(IB_2),
    .in5(Dest_Mem_Adress[3:0]), .in6(Dest_Mem_Adress[3:0]), .in7(Dest_Mem_Adress[3:0]),
    .in8(Dest_Mem_Adress[3:0]), .in9(Dest_Mem_Adress[3:0]), .in10(Dest_Mem_Adress[3:0]),
    .in11(Dest_Mem_Adress[3:0]), .in12(Dest_Mem_Adress[3:0]), .out(multiplexer_3_out), .sel(IB));  // open: in0, in13, in14, in15, en
  or or_2 (addrEnable, jump_e, Group_5);
  not not_20 (not_20_out, Clock);
  Register Address (.Clock(not_20_out), .Enable(addrEnable), .Input(multiplexer_2_out), .Output(Adress_Bus));
  Do_Jump do_jump_1 (.Instruction(Instruction), .ZF(ZF), .jump_enable(jump_e));
  Register_Bank register_bank_1 (
    .Dest_Enabler(Dest_Enabler), .Destination(multiplexer_3_out), .ALU_Output(out_15), .Clock(Clock),
    .R0(out_4), .R1(out_6), .R2(out_7), .R3(out_8), .R4(out_10), .R5(out_11), .R6(out_12), .R7(out_13));
  Decoder #(.select(4)) decoder_1 (
    .out0(Halt), .out2(RMov_Enable), .out3(decoder_1_out3), .out4(decoder_1_out4), .out5(decoder_1_out5),
    .out6(decoder_1_out6), .sel(Instruction));  // open: out1, out7, out8, out9, out10, out11, out12, out13, out14, out15, en
  or or_3 (ld_enable, decoder_1_out3, decoder_1_out4);
  or or_4 (Dest_Enabler, Group_2, Group_1, Group_3);
  or or_5 (Source_Enabler, Group_2, Group_4, Group_3);
  or or_6 (st_enable, decoder_1_out5, decoder_1_out6);
  or or_7 (or_7_out, Group_2, RMov_Enable, Group_4, Group_3);
  or or_8 (or_8_out, Group_2, Group_1, Group_3);
  Multiplexer #(.select(4), .width(8)) multiplexer_4 (
    .in1(out_4), .in2(out_6), .in3(out_7), .in4(out_8), .in5(out_10), .in6(out_11), .in7(out_12),
    .in8(out_13), .out(RagA), .sel(SMem_Adress[3:0]), .en(or_7_out));  // open: in0, in9, in10, in11, in12, in13, in14, in15
  Multiplexer #(.select(4), .width(8)) multiplexer_5 (
    .in1(out_4), .in2(out_6), .in3(out_7), .in4(out_8), .in5(out_10), .in6(out_11), .in7(out_12),
    .in8(out_13), .out(RegB), .sel(Dest_Mem_Adress[3:0]), .en(or_8_out));  // open: in0, in9, in10, in11, in12, in13, in14, in15

  assign Source = SMem_Adress[3:0];

  // Other names for the same wires on the sheet: Source_Mem_Adress[7:0] = SMem_Adress;
  //   mem_data[7:0] = {Instruction, Group}; Destination[3:0] = Dest_Mem_Adress[3:0]; Address[7:0] = Adress_Bus;
  //   Dest_4_load[3:0] = IB_2; R0[7:0] = out_4; R1[7:0] = out_6; R2[7:0] = out_7; R3[7:0] = out_8; R4[7:0] = out_10;
  //   R5[7:0] = out_11; R6[7:0] = out_12; R7[7:0] = out_13; RegA[7:0] = RagA; Src_Enabler = Source_Enabler

  // Notes on the sheet:
  //   halt
  //   IRMov
  //   help
  //   Dest Enabler
endmodule

module Register_Bank (
  input  Dest_Enabler,
  input  [3:0] Destination,
  input  Clock,
  input  [7:0] ALU_Output,
  output [7:0] R0,
  output [7:0] R1,
  output [7:0] R2,
  output [7:0] R3,
  output [7:0] R4,
  output [7:0] R5,
  output [7:0] R6,
  output [7:0] R7
);

  wire and_1_out, and_2_out, and_3_out, and_4_out, and_5_out, and_6_out, and_7_out, and_8_out,
       decoder_1_out1, decoder_1_out2, decoder_1_out3, decoder_1_out4, decoder_1_out5, decoder_1_out6,
       decoder_1_out7, decoder_1_out8, not_1_out;

  Decoder #(.select(4)) decoder_1 (
    .out1(decoder_1_out1), .out2(decoder_1_out2), .out3(decoder_1_out3), .out4(decoder_1_out4),
    .out5(decoder_1_out5), .out6(decoder_1_out6), .out7(decoder_1_out7), .out8(decoder_1_out8),
    .sel(Destination), .en(Dest_Enabler));  // open: out0, out9, out10, out11, out12, out13, out14, out15
  not not_1 (not_1_out, Clock);
  and and_1 (and_1_out, not_1_out, decoder_1_out1);
  and and_2 (and_2_out, not_1_out, decoder_1_out2);
  and and_3 (and_3_out, not_1_out, decoder_1_out3);
  and and_4 (and_4_out, not_1_out, decoder_1_out4);
  and and_5 (and_5_out, not_1_out, decoder_1_out5);
  and and_6 (and_6_out, not_1_out, decoder_1_out6);
  and and_7 (and_7_out, not_1_out, decoder_1_out7);
  and and_8 (and_8_out, not_1_out, decoder_1_out8);
  Register u_R0 (.Clock(and_1_out), .Enable(decoder_1_out1), .Input(ALU_Output), .Output(R0));
  Register u_R1 (.Clock(and_2_out), .Enable(decoder_1_out2), .Input(ALU_Output), .Output(R1));
  Register u_R2 (.Clock(and_3_out), .Enable(decoder_1_out3), .Input(ALU_Output), .Output(R2));
  Register u_R3 (.Clock(and_4_out), .Enable(decoder_1_out4), .Input(ALU_Output), .Output(R3));
  Register u_R4 (.Clock(and_5_out), .Enable(decoder_1_out5), .Input(ALU_Output), .Output(R4));
  Register u_R5 (.Clock(and_6_out), .Enable(decoder_1_out6), .Input(ALU_Output), .Output(R5));
  Register u_R6 (.Clock(and_7_out), .Enable(decoder_1_out7), .Input(ALU_Output), .Output(R6));
  Register u_R7 (.Clock(and_8_out), .Enable(decoder_1_out8), .Input(ALU_Output), .Output(R7));
endmodule

module Register (
  input  Clock,
  input  Enable,
  input  [7:0] Input,
  output [7:0] Output
);

  D_Flip_Flop d_ff_1 (.clk(Clock), .D(Input[0]), .Q(Output[0]), .en(Enable));  // open: Qn, preset, reset
  D_Flip_Flop d_ff_2 (.clk(Clock), .D(Input[1]), .Q(Output[1]), .en(Enable));  // open: Qn, preset, reset
  D_Flip_Flop d_ff_3 (.clk(Clock), .D(Input[2]), .Q(Output[2]), .en(Enable));  // open: Qn, preset, reset
  D_Flip_Flop d_ff_4 (.clk(Clock), .D(Input[3]), .Q(Output[3]), .en(Enable));  // open: Qn, preset, reset
  D_Flip_Flop d_ff_5 (.clk(Clock), .D(Input[4]), .Q(Output[4]), .en(Enable));  // open: Qn, preset, reset
  D_Flip_Flop d_ff_6 (.clk(Clock), .D(Input[5]), .Q(Output[5]), .en(Enable));  // open: Qn, preset, reset
  D_Flip_Flop d_ff_7 (.clk(Clock), .D(Input[6]), .Q(Output[6]), .en(Enable));  // open: Qn, preset, reset
  D_Flip_Flop d_ff_8 (.clk(Clock), .D(Input[7]), .Q(Output[7]), .en(Enable));  // open: Qn, preset, reset
endmodule

module ALU (
  input  [7:0] RA,
  input  [7:0] RB,
  input  str,
  input  [3:0] Instruction,
  input  ld_enable,
  input  Clock,
  output [7:0] ALU_Output,
  output [7:0] Data,
  output ZF
);

  wire not_1_out, not_2_out;
  wire [7:0] adder_1_out, multiplier_1_out, subtractor_1_out;

  not not_1 (not_1_out, ld_enable);
  Adder adder_1 (.a(RA), .b(RB), .out(adder_1_out));  // open: cin, cout
  Multiplexer #(.select(4), .width(8), .enable("false")) multiplexer_1 (
    .in1(RA), .in2(RA), .in3(RA), .in4(Data), .in5(Data), .in7(adder_1_out), .in8(subtractor_1_out),
    .in9(multiplier_1_out), .in10(Data), .in11(Data), .out(ALU_Output), .sel(Instruction));  // open: in0, in6, in12, in13, in14, in15
  not not_2 (not_2_out, Clock);
  Subtractor subtractor_1 (.a(RA), .b(RB), .out(subtractor_1_out));  // open: bin, bout
  Register u_Data (.Clock(not_2_out), .Enable(1'b1), .Input(ALU_Output), .Output(Data));
  Multiplier multiplier_1 (.a(RA), .b(RB), .out(multiplier_1_out));  // open: cin, cout
  Comparator comparator_1 (.a(Data), .b({8{1'b0}}), .eq(ZF));  // open: gt, lt

  // Other names for the same wires on the sheet: ALU_out[7:0] = ALU_Output; Reg_out[7:0] = Data

  // Notes on the sheet:
  //   Source
  //   Destination
  //   Register Values
  //   irmov
  //   rrmov
  //   Add
  //   Sub
  //   Mul
endmodule

module PC (
  input  HALT,
  input  Enabler,
  input  [7:0] Address,
  input  LD_Enable,
  output Clock,
  output [7:0] PC
);

  wire and_1_out, and_2_out;
  wire [7:0] counter_1_q, counter_2_q, demultiplexer_1_out0, demultiplexer_1_out1;

  Demultiplexer #(.width(8)) demultiplexer_1 (
    .out0(demultiplexer_1_out0), .out1(demultiplexer_1_out1), .in(Address), .sel(LD_Enable));  // open: en
  Clock clock_1 (.out(Clock));
  and and_1 (and_1_out, ~HALT, Clock);  // AND_Gate
  and and_2 (and_2_out, ~Enabler, ~LD_Enable);  // AND_Gate
  Counter counter_1 (
    .load(Enabler), .D(demultiplexer_1_out0), .count(and_2_out), .Q(counter_1_q), .clk(and_1_out));  // open: carry, clr
  Counter counter_2 (
    .load(LD_Enable), .D(demultiplexer_1_out1), .count(1'b0), .Q(counter_2_q));  // open: carry, clk, clr
  Multiplexer #(.width(8)) multiplexer_1 (.in0(counter_1_q), .in1(counter_2_q), .out(PC), .sel(LD_Enable));  // open: en
endmodule

module Do_Jump (
  input  [3:0] Instruction,
  input  ZF,
  output jump_enable
);

  wire and_1_out, and_2_out, not_1_out, not_2_out;

  not not_1 (not_1_out, Instruction[0]);
  not not_2 (not_2_out, Instruction[2]);
  and and_1 (and_1_out, not_1_out, Instruction[1], not_2_out, Instruction[3]);
  and and_2 (and_2_out, Instruction[0], Instruction[1], not_2_out, Instruction[3], ZF);
  or or_1 (jump_enable, and_1_out, and_2_out);

  // Notes on the sheet:
  //   If jmp
  //   If jz and ZF set
endmodule

module IB (
  input  Clock,
  input  [3:0] Instruction,
  output [3:0] Data
);

  wire not_1_out;
  wire [7:0] bit_extender_1_out;
  wire [7:4] IB_output;

  assign bit_extender_1_out = {{4{1'b0}}, Instruction};  // Bit_Extender bit_extender_1
  not not_1 (not_1_out, Clock);
  Register IB (.Clock(not_1_out), .Enable(1'b1), .Input(bit_extender_1_out), .Output({IB_output, Data}));
endmodule
