// Logisim project Master.circ as structural Verilog: 5 circuits, main circuit main
module main (
  input  [7:0] in_1,
  output [7:0] DMem_Adress,
  output [3:0] Source,
  output Source_Enabler,
  output [7:0] SMem_Adress,
  output [3:0] Instruction,
  output Halt,
  output [7:0] out_8,
  output [7:0] out_9,
  output [7:0] out_10,
  output Clock,
  output [7:0] out_12,
  output [7:0] out_13,
  output [7:0] out_14,
  output [7:0] out_15,
  output [7:0] out_16
);

  wire Add, and_2_out, and_4_out, and_10_out, Dest_Enabler, Group_0, Group_1, Group_2, Group_3, Group_4, Mul,
       not_1_out, not_2_out, not_3_out, not_4_out, not_5_out, not_6_out, not_7_out, not_8_out, not_9_out,
       not_10_out, not_11_out, not_12_out, not_13_out, not_14_out, not_15_out, or_3_out, or_4_out, RRMov,
       Subtract_On;
  wire [3:0] Group;
  wire [4:0] pc_1_count;
  wire [7:0] RegA, RegB;

  PC pc_1 (.Count(pc_1_count), .HALT(Halt), .Clock(Clock));
  not not_1 (not_1_out, Group[1]);
  not not_2 (not_2_out, Group[0]);
  not not_3 (not_3_out, Group[3]);
  not not_4 (not_4_out, Group[2]);
  and and_1 (Group_0, not_2_out, not_1_out, not_4_out, not_3_out);
  LED led_1 (.in(Group_0));
  and and_2 (and_2_out, Group_3, Instruction[0], Instruction[1], ~Instruction[2], ~Instruction[3]);  // AND_Gate
  LED led_2 (.in(and_2_out));
  not not_5 (not_5_out, Group[2]);
  not not_6 (not_6_out, Group[1]);
  not not_7 (not_7_out, Group[0]);
  not not_8 (not_8_out, Group[3]);
  and and_3 (Group_1, Group[0], not_6_out, not_5_out, not_8_out);
  LED led_3 (.in(Group_1));
  and and_4 (and_4_out, Group_3, ~Instruction[0], Instruction[1], Instruction[2], ~Instruction[3]);  // AND_Gate
  LED led_4 (.in(and_4_out));
  ROM #(.addrWidth(5), .dataWidth(24)) rom_1 (
    .addr(pc_1_count), .data({Group, Instruction, SMem_Adress, DMem_Adress}));  // open: sel
  not not_9 (not_9_out, Group[2]);
  not not_10 (not_10_out, Group[3]);
  and and_5 (Group_2, not_7_out, Group[1], not_9_out, not_10_out);
  and and_6 (Group_3, Group[0], Group[1], not_13_out, not_14_out);
  LED led_5 (.in(Group_3));
  LED led_6 (.in(Group_2));
  not not_11 (not_11_out, Group[0]);
  not not_12 (not_12_out, Group[1]);
  not not_13 (not_13_out, Group[2]);
  not not_14 (not_14_out, Group[3]);
  not not_15 (not_15_out, Group[3]);
  and and_7 (Group_4, not_11_out, not_12_out, Group[2], not_15_out);
  LED led_7 (.in(Group_4));
  and and_8 (Add, Group_2, Instruction[0], Instruction[1], Instruction[2], ~Instruction[3]);  // AND_Gate
  LED led_8 (.in(Add));
  and and_9 (Mul, Group_2, Instruction[0], ~Instruction[1], ~Instruction[2], Instruction[3]);  // AND_Gate
  LED led_9 (.in(Mul));
  and and_10 (and_10_out, Group_2, ~Instruction[0], ~Instruction[1], ~Instruction[2]);  // AND_Gate
  and and_11 (RRMov, Group_2, ~Instruction[0], Instruction[1], ~Instruction[2], ~Instruction[3]);  // AND_Gate
  LED led_10 (.in(and_10_out));
  LED led_11 (.in(RRMov));
  Register_Bank register_bank_1 (
    .Dest_Enabler(Dest_Enabler), .Destination(DMem_Adress[3:0]), .ALU_Output(in_1), .Clock(Clock),
    .R0(out_8), .R1(out_9), .R2(out_10), .R3(out_12), .R4(out_13), .R5(out_14), .R6(out_15), .R7(out_16));
  Decoder #(.select(4)) decoder_1 (
    .out0(Halt), .out8(Subtract_On), .sel(Instruction));  // open: out1, out2, out3, out4, out5, out6, out7, out9, out10, out11, out12, out13, out14, out15, en
  or or_1 (Dest_Enabler, Group_2, Group_1, Group_3);
  or or_2 (Source_Enabler, Group_2, Group_4, Group_3);
  or or_3 (or_3_out, Group_2, Group_4, Group_3);
  or or_4 (or_4_out, Group_2, Group_1, Group_3);
  Multiplexer #(.select(4), .width(8)) multiplexer_1 (
    .in1(out_8), .in2(out_9), .in3(out_10), .in4(out_12), .in5(out_13), .in6(out_14), .in7(out_15),
    .in8(out_16), .out(RegA), .sel(SMem_Adress[3:0]), .en(or_3_out));  // open: in0, in9, in10, in11, in12, in13, in14, in15
  Multiplexer #(.select(4), .width(8)) multiplexer_2 (
    .in1(out_8), .in2(out_9), .in3(out_10), .in4(out_12), .in5(out_13), .in6(out_14), .in7(out_15),
    .in8(out_16), .out(RegB), .sel(DMem_Adress[3:0]), .en(or_4_out));  // open: in0, in9, in10, in11, in12, in13, in14, in15

  assign Source = SMem_Adress[3:0];

  // Other names for the same wires on the sheet: Dest_Mem_Adress[7:0] = DMem_Adress;
  //   Source_Mem_Adress[7:0] = SMem_Adress; Destination[3:0] = DMem_Adress[3:0]; R0[7:0] = out_8; R1[7:0] = out_9;
  //   R2[7:0] = out_10; R3[7:0] = out_12; R4[7:0] = out_13; R5[7:0] = out_14; R6[7:0] = out_15; R7[7:0] = out_16

  // Notes on the sheet:
  //   halt
  //   ldm
  //   IRMov
  //   stm
  //   contents of rom_1 (hex, n*v repeats v):
  //   ffffff 270102 290805 115c07 220604 4bff00 4a1b00 280301 330203 5407ab 360408 5505bf
  //   Instructions
  //   help
  //   Dest Enabler
endmodule

module Register_Bank (
  input  Dest_Enabler,
  input  [3:0] Destination,
  input  Clock,
  input  [7:0] ALU_Output,
  output [7:0] R0,
  output [7:0] R1,
  output [7:0] R2,
  output [7:0] R3,
  output [7:0] R4,
  output [7:0] R5,
  output [7:0] R6,
  output [7:0] R7
);

  wire and_1_out, and_2_out, and_3_out, and_4_out, and_5_out, and_6_out, and_7_out, and_8_out,
       decoder_1_out1, decoder_1_out2, decoder_1_out3, decoder_1_out4, decoder_1_out5, decoder_1_out6,
       decoder_1_out7, decoder_1_out8, not_1_out;

  Decoder #(.select(4)) decoder_1 (
    .out1(decoder_1_out1), .out2(decoder_1_out2), .out3(decoder_1_out3), .out4(decoder_1_out4),
    .out5(decoder_1_out5), .out6(decoder_1_out6), .out7(decoder_1_out7), .out8(decoder_1_out8),
    .sel(Destination), .en(Dest_Enabler));  // open: out0, out9, out10, out11, out12, out13, out14, out15
  not not_1 (not_1_out, Clock);
  and and_1 (and_1_out, not_1_out, decoder_1_out1);
  and and_2 (and_2_out, not_1_out, decoder_1_out2);
  and and_3 (and_3_out, not_1_out, decoder_1_out3);
  and and_4 (and_4_out, not_1_out, decoder_1_out4);
  and and_5 (and_5_out, not_1_out, decoder_1_out5);
  and and_6 (and_6_out, not_1_out, decoder_1_out6);
  and and_7 (and_7_out, not_1_out, decoder_1_out7);
  and and_8 (and_8_out, not_1_out, decoder_1_out8);
  Register u_R0 (.in_1(and_1_out), .Enable(decoder_1_out1), .Input(ALU_Output), .out_4(R0));
  Register u_R1 (.in_1(and_2_out), .Enable(decoder_1_out2), .Input(ALU_Output), .out_4(R1));
  Register u_R2 (.in_1(and_3_out), .Enable(decoder_1_out3), .Input(ALU_Output), .out_4(R2));
  Register u_R3 (.in_1(and_4_out), .Enable(decoder_1_out4), .Input(ALU_Output), .out_4(R3));
  Register u_R4 (.in_1(and_5_out), .Enable(decoder_1_out5), .Input(ALU_Output), .out_4(R4));
  Register u_R5 (.in_1(and_6_out), .Enable(decoder_1_out6), .Input(ALU_Output), .out_4(R5));
  Register u_R6 (.in_1(and_7_out), .Enable(decoder_1_out7), .Input(ALU_Output), .out_4(R6));
  Register u_R7 (.in_1(and_8_out), .Enable(decoder_1_out8), .Input(ALU_Output), .out_4(R7));
endmodule

module Register (
  input  in_1,
  input  Enable,
  input  [7:0] Input,
  output [7:0] out_4
);

  D_Flip_Flop d_ff_1 (.clk(in_1), .D(Input[0]), .Q(out_4[0]), .en(Enable));  // open: Qn, preset, reset
  D_Flip_Flop d_ff_2 (.clk(in_1), .D(Input[1]), .Q(out_4[1]), .en(Enable));  // open: Qn, preset, reset
  D_Flip_Flop d_ff_3 (.clk(in_1), .D(Input[2]), .Q(out_4[2]), .en(Enable));  // open: Qn, preset, reset
  D_Flip_Flop d_ff_4 (.clk(in_1), .D(Input[3]), .Q(out_4[3]), .en(Enable));  // open: Qn, preset, reset
  D_Flip_Flop d_ff_5 (.clk(in_1), .D(Input[4]), .Q(out_4[4]), .en(Enable));  // open: Qn, preset, reset
  D_Flip_Flop d_ff_6 (.clk(in_1), .D(Input[5]), .Q(out_4[5]), .en(Enable));  // open: Qn, preset, reset
  D_Flip_Flop d_ff_7 (.clk(in_1), .D(Input[6]), .Q(out_4[6]), .en(Enable));  // open: Qn, preset, reset
  D_Flip_Flop d_ff_8 (.clk(in_1), .D(Input[7]), .Q(out_4[7]), .en(Enable));  // open: Qn, preset, reset
endmodule

module ALU (
  input  in_1,
  input  in_2,
  input  in_3,
  input  in_4,
  input  in_5,
  input  in_6,
  input  in_7,
  input  in_8,
  input  in_9,
  input  in_10,
  input  in_11,
  input  in_12,
  input  in_13,
  input  in_14,
  input  in_15,
  input  in_16,
  input  in_17,
  output [7:0] out_18
);

  wire [3:0] Instruction;
  wire [7:0] IRMov;
  wire [7:1] undriven, undriven_2, undriven_3, undriven_4, undriven_5, undriven_6, undriven_7, undriven_8,
       undriven_9, undriven_10, undriven_11, undriven_12, undriven_13, undriven_14, undriven_15;

  Multiplexer #(.select(4), .width(8)) multiplexer_1 (
    .in0({undriven, in_12}), .in1({undriven_2, in_13}), .in2({undriven_3, in_14}), .in3({undriven_4, in_15}),
    .in4({undriven_5, in_16}), .in5({undriven_6, in_2}), .in6({undriven_7, in_3}), .in7({undriven_8, in_4}),
    .in8({undriven_9, in_5}), .in9({undriven_10, in_6}), .in10({undriven_11, in_7}),
    .in11({undriven_13, in_8}), .in12({undriven_14, in_9}), .in13({undriven_12, in_10}),
    .in14({undriven_15, in_11}), .in15(IRMov), .out(out_18), .sel(Instruction), .en(in_17));
  // Pins of 1 and 8 bits meet at {undriven_6, in_2}
  // Pins of 1 and 8 bits meet at {undriven_13, in_8}
  // Pins of 1 and 8 bits meet at {undriven_10, in_6}
  // Pins of 1 and 8 bits meet at {undriven_2, in_13}
  // Pins of 1 and 8 bits meet at {undriven, in_12}
  // Pins of 1 and 8 bits meet at {undriven_3, in_14}
  // Pins of 1 and 8 bits meet at {undriven_4, in_15}
  // Pins of 1 and 8 bits meet at {undriven_5, in_16}
  // Pins of 1 and 8 bits meet at {undriven_7, in_3}
  // Pins of 1 and 8 bits meet at {undriven_8, in_4}
  // Pins of 1 and 8 bits meet at {undriven_9, in_5}
  // Pins of 1 and 8 bits meet at {undriven_11, in_7}

  // Notes on the sheet:
  //   Register Values
endmodule

module PC (
  input  HALT,
  output Clock,
  output [4:0] Count
);

  wire and_1_out, t_ff_1_qn, t_ff_2_qn, t_ff_3_qn, t_ff_4_qn;

  T_Flip_Flop t_ff_1 (.clk(and_1_out), .T(1'b1), .Q(Count[0]), .Qn(t_ff_1_qn));  // open: preset, reset, en
  Clock clock_1 (.out(Clock));
  and and_1 (and_1_out, ~HALT, Clock);  // AND_Gate
  T_Flip_Flop t_ff_2 (.clk(t_ff_1_qn), .T(1'b1), .Q(Count[1]), .Qn(t_ff_2_qn));  // open: preset, reset, en
  T_Flip_Flop t_ff_3 (.clk(t_ff_2_qn), .T(1'b1), .Q(Count[2]), .Qn(t_ff_3_qn));  // open: preset, reset, en
  T_Flip_Flop t_ff_4 (.clk(t_ff_3_qn), .T(1'b1), .Q(Count[3]), .Qn(t_ff_4_qn));  // open: preset, reset, en
  T_Flip_Flop t_ff_5 (.clk(t_ff_4_qn), .T(1'b1), .Q(Count[4]));  // open: Qn, preset, reset, en
endmodule
